// Logisim project lab01.circ as structural Verilog
module oneBitSum (
  input  S,
  input  A,
  input  B,
  output R,
  output C
);

  wire and_1_out, and_2_out, xor_1_out;

  xor xor_1 (xor_1_out, A, B);
  and and_1 (and_1_out, A, B);
  xor xor_2 (R, S, xor_1_out);
  and and_2 (and_2_out, S, xor_1_out);
  or or_1 (C, and_2_out, and_1_out);
endmodule

module eightBitSum (
  input  S,
  input  [7:0] A,
  input  [7:0] B,
  output [7:0] R,
  output C
);

  wire onebitsum_1_c, onebitsum_2_c, onebitsum_3_c, onebitsum_4_c, onebitsum_5_c, onebitsum_6_c,
       onebitsum_7_c;

  oneBitSum onebitsum_1 (.C(onebitsum_1_c), .R(R[0]), .B(B[0]), .A(A[0]), .S(S));
  oneBitSum onebitsum_2 (.C(onebitsum_2_c), .R(R[1]), .B(B[1]), .A(A[1]), .S(onebitsum_1_c));
  oneBitSum onebitsum_3 (.C(onebitsum_3_c), .R(R[2]), .B(B[2]), .A(A[2]), .S(onebitsum_2_c));
  oneBitSum onebitsum_4 (.C(onebitsum_4_c), .R(R[3]), .B(B[3]), .A(A[3]), .S(onebitsum_3_c));
  oneBitSum onebitsum_5 (.C(onebitsum_5_c), .R(R[4]), .B(B[4]), .A(A[4]), .S(onebitsum_4_c));
  oneBitSum onebitsum_6 (.C(onebitsum_6_c), .R(R[5]), .B(B[5]), .A(A[5]), .S(onebitsum_5_c));
  oneBitSum onebitsum_7 (.C(onebitsum_7_c), .R(R[6]), .B(B[6]), .A(A[6]), .S(onebitsum_6_c));
  oneBitSum onebitsum_8 (.C(C), .R(R[7]), .B(B[7]), .A(A[7]), .S(onebitsum_7_c));
endmodule
