// Logisim project lab04.circ as structural Verilog
module oneBitSum (
  input  S,
  input  A,
  input  B,
  output R,
  output C
);

  wire and_1_out, and_2_out, xor_1_out;

  xor xor_1 (xor_1_out, A, B);
  and and_1 (and_1_out, A, B);
  xor xor_2 (R, S, xor_1_out);
  and and_2 (and_2_out, S, xor_1_out);
  or or_1 (C, and_2_out, and_1_out);
endmodule

module oneBitMux (
  input  S,
  input  A,
  input  B,
  output R
);

  wire and_1_out, and_2_out, not_1_out;

  not not_1 (not_1_out, S);
  and and_1 (and_1_out, not_1_out, A);
  and and_2 (and_2_out, S, B);
  or or_1 (R, and_1_out, and_2_out);
endmodule

module eightBitSum (
  input  S,
  input  [7:0] A,
  input  [7:0] B,
  output [7:0] R,
  output C
);

  wire onebitsum_1_c, onebitsum_2_c, onebitsum_3_c, onebitsum_4_c, onebitsum_5_c, onebitsum_6_c,
       onebitsum_7_c;

  oneBitSum onebitsum_1 (.C(onebitsum_1_c), .R(R[0]), .B(B[0]), .A(A[0]), .S(S));
  oneBitSum onebitsum_2 (.C(onebitsum_2_c), .R(R[1]), .B(B[1]), .A(A[1]), .S(onebitsum_1_c));
  oneBitSum onebitsum_3 (.C(onebitsum_3_c), .R(R[2]), .B(B[2]), .A(A[2]), .S(onebitsum_2_c));
  oneBitSum onebitsum_4 (.C(onebitsum_4_c), .R(R[3]), .B(B[3]), .A(A[3]), .S(onebitsum_3_c));
  oneBitSum onebitsum_5 (.C(onebitsum_5_c), .R(R[4]), .B(B[4]), .A(A[4]), .S(onebitsum_4_c));
  oneBitSum onebitsum_6 (.C(onebitsum_6_c), .R(R[5]), .B(B[5]), .A(A[5]), .S(onebitsum_5_c));
  oneBitSum onebitsum_7 (.C(onebitsum_7_c), .R(R[6]), .B(B[6]), .A(A[6]), .S(onebitsum_6_c));
  oneBitSum onebitsum_8 (.C(C), .R(R[7]), .B(B[7]), .A(A[7]), .S(onebitsum_7_c));
endmodule

module eightBitMux (
  input  S,
  input  [7:0] A,
  input  [7:0] B,
  output [7:0] R
);

  oneBitMux onebitmux_1 (.R(R[0]), .B(B[0]), .A(A[0]), .S(S));
  oneBitMux onebitmux_2 (.R(R[1]), .B(B[1]), .A(A[1]), .S(S));
  oneBitMux onebitmux_3 (.R(R[2]), .B(B[2]), .A(A[2]), .S(S));
  oneBitMux onebitmux_4 (.R(R[3]), .B(B[3]), .A(A[3]), .S(S));
  oneBitMux onebitmux_5 (.R(R[4]), .B(B[4]), .A(A[4]), .S(S));
  oneBitMux onebitmux_6 (.R(R[5]), .B(B[5]), .A(A[5]), .S(S));
  oneBitMux onebitmux_7 (.R(R[6]), .B(B[6]), .A(A[6]), .S(S));
  oneBitMux onebitmux_8 (.R(R[7]), .B(B[7]), .A(A[7]), .S(S));
endmodule

module oneBitComparison (
  input  A,
  input  B,
  output R
);

  wire and_1_out, and_2_out, not_1_out, not_2_out;

  not not_1 (not_1_out, A);
  not not_2 (not_2_out, B);
  and and_1 (and_1_out, A, B);
  and and_2 (and_2_out, not_1_out, not_2_out);
  or or_1 (R, and_1_out, and_2_out);
endmodule

module eightBitComparison (
  input  [7:0] A,
  input  [7:0] B,
  output R
);

  wire onebitcomparison_1_r, onebitcomparison_2_r, onebitcomparison_3_r, onebitcomparison_4_r,
       onebitcomparison_5_r, onebitcomparison_6_r, onebitcomparison_7_r, onebitcomparison_8_r;

  oneBitComparison onebitcomparison_1 (.A(A[0]), .B(B[0]), .R(onebitcomparison_1_r));
  oneBitComparison onebitcomparison_2 (.A(A[1]), .B(B[1]), .R(onebitcomparison_2_r));
  oneBitComparison onebitcomparison_3 (.A(A[2]), .B(B[2]), .R(onebitcomparison_3_r));
  oneBitComparison onebitcomparison_4 (.A(A[3]), .B(B[3]), .R(onebitcomparison_4_r));
  oneBitComparison onebitcomparison_5 (.A(A[4]), .B(B[4]), .R(onebitcomparison_5_r));
  oneBitComparison onebitcomparison_6 (.A(A[5]), .B(B[5]), .R(onebitcomparison_6_r));
  oneBitComparison onebitcomparison_7 (.A(A[6]), .B(B[6]), .R(onebitcomparison_7_r));
  oneBitComparison onebitcomparison_8 (.A(A[7]), .B(B[7]), .R(onebitcomparison_8_r));
  and and_1 (R, onebitcomparison_1_r, onebitcomparison_2_r, onebitcomparison_3_r, onebitcomparison_4_r, onebitcomparison_5_r, onebitcomparison_6_r, onebitcomparison_7_r, onebitcomparison_8_r);
endmodule

module muxResta (
  input  in_1,
  input  in_2,
  input  in_3,
  output out_4,
  output out_5
);

  wire not_1_out, onebitmux_1_r;

  not not_1 (not_1_out, in_3);
  oneBitMux onebitmux_1 (.R(onebitmux_1_r), .B(not_1_out), .A(in_3), .S(in_1));
  oneBitSum onebitsum_1 (.C(out_5), .R(out_4), .B(onebitmux_1_r), .A(in_2), .S(in_1));
endmodule

module eightBitResta (
  input  S,
  input  [7:0] A,
  input  [7:0] B,
  output [7:0] R,
  output C
);

  wire [7:0] eightbitmux_1_r, not_1_out;

  assign not_1_out = ~B;  // NOT_Gate not_1, 8 bits wide
  eightBitMux eightbitmux_1 (.R(eightbitmux_1_r), .B(not_1_out), .A(B), .S(S));
  eightBitSum eightbitsum_1 (.C(C), .R(R), .B(eightbitmux_1_r), .A(A), .S(S));
endmodule

module bono (
  input  [1:0] op,
  input  [7:0] A,
  input  [7:0] B,
  input  [6:0] in_4,
  output [7:0] R,
  output C
);

  wire [0:0] eightbitcomparison_1_r;
  wire [7:0] eightbitmux_1_r, eightbitsum_1_r, not_1_out;

  assign not_1_out = ~B;  // NOT_Gate not_1, 8 bits wide
  eightBitMux eightbitmux_1 (.R(eightbitmux_1_r), .B(not_1_out), .A(B), .S(op[0]));
  eightBitSum eightbitsum_1 (.C(C), .R(eightbitsum_1_r), .B(eightbitmux_1_r), .A(A), .S(op[0]));
  eightBitComparison eightbitcomparison_1 (.R(eightbitcomparison_1_r[0]), .B(eightbitmux_1_r), .A(A));
  eightBitMux eightbitmux_2 (.R(R), .B({in_4, eightbitcomparison_1_r[0]}), .A(eightbitsum_1_r), .S(op[1]));
endmodule
