// Logisim project lab1.circ as structural Verilog
module oneBitSum (
  input  s,
  input  a,
  input  b,
  output r,
  output c
);

  wire and_1_out, and_2_out, xor_1_out;

  xor xor_1 (xor_1_out, a, b);
  and and_1 (and_1_out, a, b);
  xor xor_2 (r, s, xor_1_out);
  and and_2 (and_2_out, s, xor_1_out);
  or or_1 (c, and_2_out, and_1_out);
endmodule

module eightBitSum (
  input  S,
  input  [7:0] A,
  input  [7:0] B,
  output [7:0] R,
  output C
);

  wire onebitsum_1_c, onebitsum_2_c, onebitsum_3_c, onebitsum_4_c, onebitsum_5_c, onebitsum_6_c,
       onebitsum_7_c;

  oneBitSum onebitsum_1 (.c(onebitsum_1_c), .r(R[0]), .b(B[0]), .a(A[0]), .s(S));
  oneBitSum onebitsum_2 (.c(onebitsum_2_c), .r(R[1]), .b(B[1]), .a(A[1]), .s(onebitsum_1_c));
  oneBitSum onebitsum_3 (.c(onebitsum_3_c), .r(R[2]), .b(B[2]), .a(A[2]), .s(onebitsum_2_c));
  oneBitSum onebitsum_4 (.c(onebitsum_4_c), .r(R[3]), .b(B[3]), .a(A[3]), .s(onebitsum_3_c));
  oneBitSum onebitsum_5 (.c(onebitsum_5_c), .r(R[4]), .b(B[4]), .a(A[4]), .s(onebitsum_4_c));
  oneBitSum onebitsum_6 (.c(onebitsum_6_c), .r(R[5]), .b(B[5]), .a(A[5]), .s(onebitsum_5_c));
  oneBitSum onebitsum_7 (.c(onebitsum_7_c), .r(R[6]), .b(B[6]), .a(A[6]), .s(onebitsum_6_c));
  oneBitSum onebitsum_8 (.c(C), .r(R[7]), .b(B[7]), .a(A[7]), .s(onebitsum_7_c));
endmodule

module muxResta (
  input  in_1,
  input  in_2,
  input  in_3,
  output out_4,
  output out_5
);

  wire muxcircuit_1_r, not_1_out;

  not not_1 (not_1_out, in_3);
  MuxCircuit muxcircuit_1 (.R(muxcircuit_1_r), .B(not_1_out), .A(in_3), .S(in_1));
  oneBitSum onebitsum_1 (.c(out_5), .r(out_4), .b(muxcircuit_1_r), .a(in_2), .s(in_1));
endmodule

module MuxCircuit (
  input  S,
  input  A,
  input  B,
  output R
);

  wire and_1_out, and_2_out, not_1_out;

  not not_1 (not_1_out, S);
  and and_1 (and_1_out, not_1_out, A);
  and and_2 (and_2_out, S, B);
  or or_1 (R, and_1_out, and_2_out);
endmodule
