// Logisim project lab2.circ as structural Verilog
module oneBitComparison (
  input  A,
  input  B,
  output R
);

  wire and_1_out, and_2_out, not_1_out, not_2_out;

  not not_1 (not_1_out, A);
  not not_2 (not_2_out, B);
  and and_1 (and_1_out, A, B);
  and and_2 (and_2_out, not_1_out, not_2_out);
  or or_1 (R, and_1_out, and_2_out);
endmodule

module eightBitCirc (
  input  [7:0] A,
  input  [7:0] B,
  output R
);

  wire xnor_1_out, xnor_2_out, xnor_3_out, xnor_4_out, xnor_5_out, xnor_6_out, xnor_7_out, xnor_8_out;

  xnor xnor_1 (xnor_1_out, A[0], B[0]);
  xnor xnor_2 (xnor_2_out, A[1], B[1]);
  xnor xnor_3 (xnor_3_out, A[2], B[2]);
  xnor xnor_4 (xnor_4_out, A[3], B[3]);
  xnor xnor_5 (xnor_5_out, A[4], B[4]);
  xnor xnor_6 (xnor_6_out, A[5], B[5]);
  xnor xnor_7 (xnor_7_out, A[6], B[6]);
  xnor xnor_8 (xnor_8_out, A[7], B[7]);
  and and_1 (R, xnor_1_out, xnor_2_out, xnor_3_out, xnor_4_out, xnor_5_out, xnor_6_out, xnor_7_out, xnor_8_out);
endmodule

module eightBitComparison (
  input  [7:0] in_1,
  input  [7:0] in_2,
  input  [7:0] A,
  input  [7:0] B,
  output out_5,
  output R
);

  wire onebitcomparison_1_r, onebitcomparison_2_r, onebitcomparison_3_r, onebitcomparison_4_r,
       onebitcomparison_5_r, onebitcomparison_6_r, onebitcomparison_7_r, onebitcomparison_8_r;

  eightBitCirc eightbitcirc_1 (.A(in_1), .B(in_2), .R(out_5));
  oneBitComparison onebitcomparison_1 (.A(A[0]), .B(B[0]), .R(onebitcomparison_1_r));
  oneBitComparison onebitcomparison_2 (.A(A[1]), .B(B[1]), .R(onebitcomparison_2_r));
  oneBitComparison onebitcomparison_3 (.A(A[2]), .B(B[2]), .R(onebitcomparison_3_r));
  oneBitComparison onebitcomparison_4 (.A(A[3]), .B(B[3]), .R(onebitcomparison_4_r));
  oneBitComparison onebitcomparison_5 (.A(A[4]), .B(B[4]), .R(onebitcomparison_5_r));
  oneBitComparison onebitcomparison_6 (.A(A[5]), .B(B[5]), .R(onebitcomparison_6_r));
  oneBitComparison onebitcomparison_7 (.A(A[6]), .B(B[6]), .R(onebitcomparison_7_r));
  oneBitComparison onebitcomparison_8 (.A(A[7]), .B(B[7]), .R(onebitcomparison_8_r));
  and and_1 (R, onebitcomparison_1_r, onebitcomparison_2_r, onebitcomparison_3_r, onebitcomparison_4_r, onebitcomparison_5_r, onebitcomparison_6_r, onebitcomparison_7_r, onebitcomparison_8_r);
endmodule
