// Logisim project lab3.circ as structural Verilog
module oneBitMux (
  input  S,
  input  A,
  input  B,
  output R
);

  wire and_1_out, and_2_out, not_1_out;

  not not_1 (not_1_out, S);
  and and_1 (and_1_out, not_1_out, A);
  and and_2 (and_2_out, S, B);
  or or_1 (R, and_1_out, and_2_out);
endmodule

module eightBitMux (
  input  S,
  input  [7:0] A,
  input  [7:0] B,
  output [7:0] R
);

  oneBitMux onebitmux_1 (.R(R[0]), .B(B[0]), .A(A[0]), .S(S));
  oneBitMux onebitmux_2 (.R(R[1]), .B(B[1]), .A(A[1]), .S(S));
  oneBitMux onebitmux_3 (.R(R[2]), .B(B[2]), .A(A[2]), .S(S));
  oneBitMux onebitmux_4 (.R(R[3]), .B(B[3]), .A(A[3]), .S(S));
  oneBitMux onebitmux_5 (.R(R[4]), .B(B[4]), .A(A[4]), .S(S));
  oneBitMux onebitmux_6 (.R(R[5]), .B(B[5]), .A(A[5]), .S(S));
  oneBitMux onebitmux_7 (.R(R[6]), .B(B[6]), .A(A[6]), .S(S));
  oneBitMux onebitmux_8 (.R(R[7]), .B(B[7]), .A(A[7]), .S(S));
endmodule
