// Logisim project y86_cpu_distrib.circ as structural Verilog: 11 circuits, main circuit main
module main (
  output [15:0] Addr,
  output [15:0] valM,
  output [15:0] Data,
  output Cnd,
  output [15:0] valE,
  output [2:0] CC,
  output [2:0] ALU_CC,
  output [3:0] ALU_fun,
  output [15:0] ALU_A,
  output [15:0] ALU_B,
  output [15:0] Rax,
  output [15:0] Rcx,
  output [15:0] Rdx,
  output [15:0] Rbx,
  output [15:0] valA,
  output [15:0] valB,
  output [15:0] Rsp,
  output [15:0] Rbp,
  output [3:0] dstE,
  output [3:0] dstM,
  output [3:0] srcA,
  output [3:0] srcB,
  output CLKout,
  output [3:0] icode,
  output [3:0] ifun,
  output [3:0] rA,
  output [3:0] rB,
  output [15:0] valC,
  output [15:0] valP,
  output [15:0] PC,
  output [15:0] newPC,
  output [15:0] CLKcount,
  output halt,
  output [31:0] Instruction
);

  wire memorycontrol_1_memread, memorycontrol_1_memwrite, RST;

  Clock CLK (.out(CLKout));
  Button u_RST (.out(RST));
  ConditionControl conditioncontrol_1 (
    .Cnd(Cnd), .icode(icode), .ifun(ifun), .CC(CC), .CLK(CLKout), .RST(RST), .ALU_CC(ALU_CC));
  SimpleCounter simplecounter_1 (.CLK(CLKout), .RST(RST), .CountOut(CLKcount));
  RegisterFile registerfile_1 (
    .dstE(dstE), .dstM(dstM), .srcA(srcA), .srcB(srcB), .valE(valE), .valM(valM), .valA(valA), .valB(valB),
    .CLK(CLKout), .RST(RST), .Rax(Rax), .Rcx(Rcx), .Rdx(Rdx), .Rbx(Rbx), .Rsp(Rsp), .Rbp(Rbp));  // open: Rsi, Rdi
  RegisterControl registercontrol_1 (
    .dstE(dstE), .dstM(dstM), .srcA(srcA), .srcB(srcB), .icode(icode), .rA(rA), .rB(rB), .Cnd(Cnd));
  PC_Update pc_update_1 (
    .valP(valP), .icode(icode), .Cnd(Cnd), .valC(valC), .valM(valM), .oldPC(PC), .newPC(newPC), .HLT(halt));
  ALU_16b alu_16b_1 (.ALU_A(ALU_A), .ALU_B(ALU_B), .valE(valE), .CC(ALU_CC), .ALU_fun(ALU_fun));
  ALU_Control alu_control_1 (
    .ALU_A(ALU_A), .ALU_B(ALU_B), .icode(icode), .valA(valA), .valB(valB), .valC(valC), .ALU_fun(ALU_fun),
    .ifun(ifun));
  Register #(.width(16)) register_1 (.D(newPC), .en(1'b1), .clk(CLKout), .Q(PC), .clr(RST));
  // Probe on valM
  // Probe on valE
  // ROM8 #(.addrWidth(16), .outPorts(4), .memdataFont("Dialog plain 12")) InstructionMemory: pin names not known; wires that end beside it: newPC, PC, Instruction[31:24], Instruction[23:16], Instruction[15:8], Instruction[7:0]
  MemoryControl memorycontrol_1 (
    .Addr(Addr), .Data(Data), .MemWrite(memorycontrol_1_memwrite), .MemRead(memorycontrol_1_memread),
    .icode(icode), .valA(valA), .valP(valP), .valE(valE));
  RAM #(.addrWidth(16), .dataWidth(16), .databus("bibus")) DataMemory (
    .addr(Addr), .we(memorycontrol_1_memwrite), .oe(memorycontrol_1_memread), .clk(CLKout), .din(Data),
    .dout(valM));
  // Probe on icode
  Fetch fetch_1 (
    .I_0(Instruction[31:24]), .I_1(Instruction[23:16]), .I_2(Instruction[15:8]), .I_3(Instruction[7:0]),
    .icode(icode), .ifun(ifun), .rA(rA), .rB(rB), .valC(valC));
  // Probe on ifun
  // Probe on rA
  // Probe on rB
  // Probe on valC

  // Other names for the same wires on the sheet: CLK = CLKout

  // Notes on the sheet:
  //   Memory
  //   Execute
  //   PC
  //   contents of InstructionMemory (hex, n*v repeats v):
  //   10 30 f0 f3 0 30 f1 ee ff 30 f2 f 0 20 13 10 60 23 61 20 62 21 63 2 10 30 f0 2 0 30 f3 f3 0 40 30 0
  //   0 30 f3 0 0 50 13 0 0 10 63 33 30 f1 1 0 30 f2 4 0 70 41 0 60 13 40 33 0 0 20 30 61 20 71 3b 0 10 30
  //   f4 20 0 80 5e 0 62 0 23 1 10*0 a0 3f 30 f0 0 0 20 3 30 f1 3 0 70 80 0 60 30 30 f5 1 0 60 53 70 80
  //   9*0 20 32 61 12 72 6d 0 b0 3f 90
  //   Decode
  //   Write-back
  //   ifun:
  //   0: add   /  jmp
  //   1: sub   /  jle
  //   2: and   /  jl
  //   3: xor   /  je
  //   Fetch
  //   Read value should update
  //   as soon as Addr changes
  //   If not, check version of logisim
  //   icode:
  //   0: halt
  //   4: jne
  //   5: jge
  //   1: nop
  //   6: jg
  //   2: cmov, rrmov
  //   3: irmov
  //   4: rmmov
  //   5: mrmov
  //   6: OPx
  //   7: jump
  //   8: call
  //   9: ret
  //   a: push
  //   b: pop
endmodule

module MemoryControl (
  input  [3:0] icode,
  input  [15:0] valE,
  input  [15:0] valA,
  input  [15:0] valP,
  output [15:0] Addr,
  output [15:0] Data,
  output MemWrite,
  output MemRead
);

  wire [1:0] Addr_ctrl, Data_ctrl;

  ROM #(.addrWidth(4), .dataWidth(2)) rom_1 (.addr(icode), .data(Addr_ctrl));
  Multiplexer #(.select(2), .width(16), .enable("false")) multiplexer_1 (
    .in1(valE), .in2(valA), .out(Addr), .sel(Addr_ctrl));  // open: in0, in3
  Multiplexer #(.select(2), .width(16), .enable("false")) multiplexer_2 (
    .in1(valA), .in2(valP), .out(Data), .sel(Data_ctrl));  // open: in0, in3
  ROM #(.addrWidth(4), .dataWidth(2)) rom_2 (.addr(icode), .data(Data_ctrl));
  ROM #(.addrWidth(4), .dataWidth(1)) rom_3 (.addr(icode));  // open: data
  ROM #(.addrWidth(4), .dataWidth(1)) rom_4 (.addr(icode));  // open: data

  // Notes on the sheet:
  //   contents of rom_1 (hex, n*v repeats v):
  //   4*3 1 1 3 3 1 2 1 2
  //   TODO: Define los inputs para Addr y Data
  //   TODO: Define para cuales instrucciones se escribe o se lee de memoria
  //   contents of rom_2 (hex, n*v repeats v):
  //   4*3 1 3 3 3 2 3 1 3
  //   contents of rom_3 (hex, n*v repeats v):
  //   4*0 1 0 0 0 1 0 1
  //   contents of rom_4 (hex, n*v repeats v):
  //   9*0 1 0 1
endmodule

module ConditionControl (
  input  [2:0] ALU_CC,
  input  CLK,
  input  RST,
  input  [3:0] ifun,
  input  [3:0] icode,
  output Cnd,
  output [2:0] CC
);

  wire and_1_out, not_1_out, not_2_out, not_3_out, not_4_out, or_1_out, set_cc, xor_1_out, xor_2_out,
       xor_3_out, xor_4_out;

  Comparator #(.width(4)) comparator_1 (.a(icode), .b(4'b0110), .eq(set_cc));  // open: gt, lt
  xor xor_1 (xor_1_out, CC[1], CC[0]);
  xor xor_2 (xor_2_out, CC[1], CC[0]);
  xor xor_3 (xor_3_out, CC[1], CC[0]);
  xor xor_4 (xor_4_out, CC[1], CC[0]);
  Register #(.width(3)) RegCC (.D(ALU_CC), .en(set_cc), .clk(CLK), .Q(CC), .clr(RST));
  not not_1 (not_1_out, CC[2]);
  not not_2 (not_2_out, xor_3_out);
  not not_3 (not_3_out, xor_4_out);
  not not_4 (not_4_out, CC[2]);
  or or_1 (or_1_out, CC[2], xor_1_out);
  and and_1 (and_1_out, not_3_out, not_4_out);
  Multiplexer #(.select(4), .enable("false")) multiplexer_1 (
    .in0(1'b1), .in1(or_1_out), .in2(xor_2_out), .in3(CC[2]), .in4(not_1_out), .in5(not_2_out),
    .in6(and_1_out), .out(Cnd), .sel(ifun));  // open: in7, in8, in9, in10, in11, in12, in13, in14, in15

  // Other names for the same wires on the sheet: CC_OF = CC[0]; CC_SF = CC[1]; CC_ZF = CC[2]

  // Notes on the sheet:
  //   Use CC_OF, CC_SF, CC_ZF signals
  //   Combine them using gates
  //   Store CC only with arithmetic operation
  //   3: je
  //   Example
  //   4: jne
  //   5: jge
  //   6: jg
  //   0: jmp
  //   1: jle
  //   2: jl
  //   TODO: Completa las condiciones par los jumps y los cmovs
  //   <----
  //   Jump always use CC from previous cycle
  //   Input from ALU_16b
endmodule

module ALU_16b (
  input  [15:0] ALU_A,
  input  [15:0] ALU_B,
  input  [3:0] ALU_fun,
  output [2:0] CC,
  output [15:0] valE
);

  wire [15:0] adder_1_out, and_1_out, subtractor_1_out, xor_1_out;

  // Probe on ALU_A
  // Probe on ALU_B
  Adder #(.width(16)) adder_1 (.a(ALU_B), .b(ALU_A), .out(adder_1_out));  // open: cin, cout
  Subtractor #(.width(16)) subtractor_1 (.a(ALU_B), .b(ALU_A), .out(subtractor_1_out));  // open: bin, bout
  assign and_1_out = ALU_B & ALU_A;  // AND_Gate and_1, 16 bits wide
  assign xor_1_out = ALU_B ^ ALU_A;  // XOR_Gate xor_1, 16 bits wide
  Multiplexer #(.select(4), .width(16), .enable("false")) multiplexer_1 (
    .in0(adder_1_out), .in1(subtractor_1_out), .in2(and_1_out), .in3(xor_1_out), .out(valE), .sel(ALU_fun));  // open: in4, in5, in6, in7, in8, in9, in10, in11, in12, in13, in14, in15
  // Probe on ALU_fun
  Comparator #(.width(16)) comparator_1 (.a(ALU_A));  // open: b, gt, eq, lt
  Comparator #(.width(16)) comparator_2 (.a(valE), .b({16{1'b0}}), .eq(CC[2]), .lt(CC[1]));  // open: gt
  // Probe on valE

  // Other names for the same wires on the sheet: A[15:0] = ALU_A; B[15:0] = ALU_B; CC_OF = CC[0]; CC_SF = CC[1];
  //   CC_ZF = CC[2]

  // Notes on the sheet:
  //   addw rA,rB
  //   rB <- rB + rA
  //   TODO: Completa las operaciones que le faltan al ALU
  //   Overflow
  //   Signed
  //   Zero
  //   ALU
  //   TODO: Computa los Conditional Codes OF, SF, ZF
endmodule

module ALU_Control (
  input  [3:0] icode,
  input  [15:0] valA,
  input  [15:0] valB,
  input  [15:0] valC,
  input  [3:0] ifun,
  output [15:0] ALU_A,
  output [15:0] ALU_B,
  output [3:0] ALU_fun
);

  wire comparator_1_eq;
  wire [1:0] ALU_B_ctrl;
  wire [2:0] ALU_A_ctrl;

  ROM #(.addrWidth(4), .dataWidth(3)) u_ALU_A_ctrl (.addr(icode), .data(ALU_A_ctrl));
  Multiplexer #(.select(3), .width(16), .enable("false")) multiplexer_1 (
    .in0(valC), .in1(valA), .in2(16'h2), .in3(16'hfffe), .out(ALU_A), .sel(ALU_A_ctrl));  // open: in4, in5, in6, in7
  Multiplexer #(.select(2), .width(16), .enable("false")) multiplexer_2 (
    .in0({16{1'b0}}), .in1(valB), .out(ALU_B), .sel(ALU_B_ctrl));  // open: in2, in3
  ROM #(.addrWidth(4), .dataWidth(2)) rom_1 (.addr(icode), .data(ALU_B_ctrl));
  Multiplexer #(.width(4), .enable("false")) multiplexer_3 (
    .in0(4'b0000), .in1(ifun), .out(ALU_fun), .sel(comparator_1_eq));
  Comparator #(.width(4)) comparator_1 (.a(icode), .b(4'b0110), .eq(comparator_1_eq));  // open: gt, lt

  // Notes on the sheet:
  //   contents of ALU_A_ctrl (hex, n*v repeats v):
  //   7 7 1 0 0 0 1 7 3 2 3 2
  //   0: valC, 1: valA
  //   TODO: Edita los ROMs para definir los valores de ALU_A y ALU_B de acuerdo a icode
  //   ALU_A_ctrl == 7 y ALU_B_ctrl == 3 corresponde a output no definido (xxxx)
  //   contents of rom_1 (hex, n*v repeats v):
  //   3 3 0 0 1 1 1 3 4*1
  //   ALU_fun=ifun if icode==6
  //   isOP
  //   0: 0, 1: valB
endmodule

module RegisterFile (
  input  [15:0] valE,
  input  [15:0] valM,
  input  [3:0] dstE,
  input  [3:0] dstM,
  input  [3:0] srcA,
  input  [3:0] srcB,
  input  CLK,
  input  RST,
  output [15:0] valA,
  output [15:0] valB,
  output [15:0] Rax,
  output [15:0] Rcx,
  output [15:0] Rdx,
  output [15:0] Rbx,
  output [15:0] Rsp,
  output [15:0] Rbp,
  output [15:0] Rsi,
  output [15:0] Rdi
);

  wire internalregselector_1_w, internalregselector_2_w, internalregselector_3_w, internalregselector_4_w,
       internalregselector_5_w, internalregselector_6_w, internalregselector_7_w, internalregselector_8_w;
  wire [3:0] internalregselector_1_id1_out, internalregselector_1_id2_out, internalregselector_2_id1_out,
       internalregselector_2_id2_out, internalregselector_3_id1_out, internalregselector_3_id2_out,
       internalregselector_4_id1_out, internalregselector_4_id2_out, internalregselector_5_id1_out,
       internalregselector_5_id2_out, internalregselector_6_id1_out, internalregselector_6_id2_out,
       internalregselector_7_id1_out, internalregselector_7_id2_out, internalregselector_8_id1_out,
       internalregselector_8_id2_out;
  wire [15:0] internalregselector_1_val, internalregselector_1_val1_out, internalregselector_1_val2_out,
       internalregselector_2_val, internalregselector_2_val1_out, internalregselector_2_val2_out,
       internalregselector_3_val, internalregselector_3_val1_out, internalregselector_3_val2_out,
       internalregselector_4_val, internalregselector_4_val1_out, internalregselector_4_val2_out,
       internalregselector_5_val, internalregselector_5_val1_out, internalregselector_5_val2_out,
       internalregselector_6_val, internalregselector_6_val1_out, internalregselector_6_val2_out,
       internalregselector_7_val, internalregselector_7_val1_out, internalregselector_7_val2_out,
       internalregselector_8_val, internalregselector_8_val1_out, internalregselector_8_val2_out;

  InternalRegSelector internalregselector_1 (
    .myID(4'b0000), .id1(dstE), .id2(dstM), .val1(valE), .val2(valM), .W(internalregselector_1_w),
    .val(internalregselector_1_val), .id1_out(internalregselector_1_id1_out),
    .id2_out(internalregselector_1_id2_out), .val1_out(internalregselector_1_val1_out),
    .val2_out(internalregselector_1_val2_out));
  InternalRegSelector internalregselector_2 (
    .myID(4'b0001), .id1(internalregselector_1_id1_out), .id2(internalregselector_1_id2_out),
    .val1(internalregselector_1_val1_out), .val2(internalregselector_1_val2_out),
    .W(internalregselector_2_w), .val(internalregselector_2_val), .id1_out(internalregselector_2_id1_out),
    .id2_out(internalregselector_2_id2_out), .val1_out(internalregselector_2_val1_out),
    .val2_out(internalregselector_2_val2_out));
  InternalRegSelector internalregselector_3 (
    .myID(4'b0010), .id1(internalregselector_2_id1_out), .id2(internalregselector_2_id2_out),
    .val1(internalregselector_2_val1_out), .val2(internalregselector_2_val2_out),
    .W(internalregselector_3_w), .val(internalregselector_3_val), .id1_out(internalregselector_3_id1_out),
    .id2_out(internalregselector_3_id2_out), .val1_out(internalregselector_3_val1_out),
    .val2_out(internalregselector_3_val2_out));
  InternalRegSelector internalregselector_4 (
    .myID(4'b0011), .id1(internalregselector_3_id1_out), .id2(internalregselector_3_id2_out),
    .val1(internalregselector_3_val1_out), .val2(internalregselector_3_val2_out),
    .W(internalregselector_4_w), .val(internalregselector_4_val), .id1_out(internalregselector_4_id1_out),
    .id2_out(internalregselector_4_id2_out), .val1_out(internalregselector_4_val1_out),
    .val2_out(internalregselector_4_val2_out));
  InternalRegSelector internalregselector_5 (
    .myID(4'b0100), .id1(internalregselector_4_id1_out), .id2(internalregselector_4_id2_out),
    .val1(internalregselector_4_val1_out), .val2(internalregselector_4_val2_out),
    .W(internalregselector_5_w), .val(internalregselector_5_val), .id1_out(internalregselector_5_id1_out),
    .id2_out(internalregselector_5_id2_out), .val1_out(internalregselector_5_val1_out),
    .val2_out(internalregselector_5_val2_out));
  InternalRegSelector internalregselector_6 (
    .myID(4'b0101), .id1(internalregselector_5_id1_out), .id2(internalregselector_5_id2_out),
    .val1(internalregselector_5_val1_out), .val2(internalregselector_5_val2_out),
    .W(internalregselector_6_w), .val(internalregselector_6_val), .id1_out(internalregselector_6_id1_out),
    .id2_out(internalregselector_6_id2_out), .val1_out(internalregselector_6_val1_out),
    .val2_out(internalregselector_6_val2_out));
  InternalRegSelector internalregselector_7 (
    .myID(4'b0110), .id1(internalregselector_6_id1_out), .id2(internalregselector_6_id2_out),
    .val1(internalregselector_6_val1_out), .val2(internalregselector_6_val2_out),
    .W(internalregselector_7_w), .val(internalregselector_7_val), .id1_out(internalregselector_7_id1_out),
    .id2_out(internalregselector_7_id2_out), .val1_out(internalregselector_7_val1_out),
    .val2_out(internalregselector_7_val2_out));
  InternalRegSelector internalregselector_8 (
    .myID(4'b0111), .id1(internalregselector_7_id1_out), .id2(internalregselector_7_id2_out),
    .val1(internalregselector_7_val1_out), .val2(internalregselector_7_val2_out),
    .W(internalregselector_8_w), .val(internalregselector_8_val), .id1_out(internalregselector_8_id1_out),
    .id2_out(internalregselector_8_id2_out), .val1_out(internalregselector_8_val1_out),
    .val2_out(internalregselector_8_val2_out));
  Register #(.width(16)) r0_ax (
    .D(internalregselector_1_val), .en(internalregselector_1_w), .clk(CLK), .Q(Rax), .clr(RST));
  // Probe on internalregselector_1_val
  Register #(.width(16)) r1_cx (
    .D(internalregselector_2_val), .en(internalregselector_2_w), .clk(CLK), .Q(Rcx), .clr(RST));
  // Probe on internalregselector_2_val
  Register #(.width(16)) r2_dx (
    .D(internalregselector_3_val), .en(internalregselector_3_w), .clk(CLK), .Q(Rdx), .clr(RST));
  // Probe on internalregselector_3_val
  Register #(.width(16)) r3_bx (
    .D(internalregselector_4_val), .en(internalregselector_4_w), .clk(CLK), .Q(Rbx), .clr(RST));
  // Probe on internalregselector_4_val
  Register #(.width(16)) r4_sp (
    .D(internalregselector_5_val), .en(internalregselector_5_w), .clk(CLK), .Q(Rsp), .clr(RST));
  // Probe on internalregselector_5_val
  Register #(.width(16)) r5_bp (
    .D(internalregselector_6_val), .en(internalregselector_6_w), .clk(CLK), .Q(Rbp), .clr(RST));
  // Probe on internalregselector_6_val
  Register #(.width(16)) r6_si (
    .D(internalregselector_7_val), .en(internalregselector_7_w), .clk(CLK), .Q(Rsi), .clr(RST));
  // Probe on internalregselector_7_val
  Register #(.width(16)) r7_di (
    .D(internalregselector_8_val), .en(internalregselector_8_w), .clk(CLK), .Q(Rdi), .clr(RST));
  // Probe on internalregselector_8_val
  // Probe on srcA
  Multiplexer #(.select(4), .width(16), .enable("false")) multiplexer_1 (
    .in0(Rax), .in1(Rcx), .in2(Rdx), .in3(Rbx), .in4(Rsp), .in5(Rbp), .in6(Rsi), .in7(Rdi), .out(valA),
    .sel(srcA));  // open: in8, in9, in10, in11, in12, in13, in14, in15
  // Probe on srcB
  Multiplexer #(.select(4), .width(16), .enable("false")) multiplexer_2 (
    .in0(Rax), .in1(Rcx), .in2(Rdx), .in3(Rbx), .in4(Rsp), .in5(Rbp), .in6(Rsi), .in7(Rdi), .out(valB),
    .sel(srcB));  // open: in8, in9, in10, in11, in12, in13, in14, in15

  // Notes on the sheet:
  //   Not need to edit, unless you want to add registers at the bottom
  //   Could add more registers following the same template
endmodule

module InternalRegSelector (
  input  [3:0] id1,
  input  [3:0] id2,
  input  [15:0] val1,
  input  [15:0] val2,
  input  [3:0] myID,
  output [3:0] id1_out,
  output [3:0] id2_out,
  output [15:0] val1_out,
  output [15:0] val2_out,
  output [15:0] val,
  output W
);

  wire [1:0] comparator_1_eq;
  wire [15:0] pull_resistor_1_node;

  Comparator #(.width(4)) comparator_1 (.a(id1), .b(myID), .eq(comparator_1_eq[0]));  // open: gt, lt
  Comparator #(.width(4)) comparator_2 (.a(id2), .b(myID), .eq(comparator_1_eq[1]));  // open: gt, lt
  or or_1 (W, comparator_1_eq[0], comparator_1_eq[1]);
  Pull_Resistor #(.pull("X")) pull_resistor_1 (.node(pull_resistor_1_node));
  Multiplexer #(.select(2), .width(16), .enable("false")) multiplexer_1 (
    .in0(pull_resistor_1_node), .in1(val1), .in2(val2), .in3(val2), .out(val), .sel(comparator_1_eq));
  // Probe on comparator_1_eq

  assign id1_out = id1;
  assign id2_out = id2;
  assign val1_out = val1;
  assign val2_out = val2;

  // Notes on the sheet:
  //   Internal module for RegisterFile: DO NOT EDIT
  //   E
  //   M
  //   This can occur for pop %sp
  //   Note: in case of conflict (simultaneous writes)
  //   port 2 has priority (valM) (see practice exercice 4.22)
endmodule

module RegisterControl (
  input  Cnd,
  input  [3:0] icode,
  input  [3:0] rA,
  input  [3:0] rB,
  output [3:0] dstE,
  output [3:0] dstM,
  output [3:0] srcA,
  output [3:0] srcB
);

  wire [1:0] dstE_ctrl, dstM_ctrl, srcA_ctrl, srcB_ctrl;

  ROM #(.addrWidth(4), .dataWidth(2)) rom_1 (.addr(icode), .data(dstE_ctrl));
  ROM #(.addrWidth(4), .dataWidth(2)) rom_2 (.addr(icode), .data(dstM_ctrl));
  // Probe on dstE_ctrl
  Multiplexer #(.select(2), .width(4), .enable("false")) multiplexer_1 (
    .in0(rB), .in1(4'b0100), .in3(4'b1111), .out(dstE), .sel(dstE_ctrl));  // open: in2
  // Probe on dstM_ctrl
  // Probe on dstE_ctrl
  // Probe on dstM_ctrl
  Multiplexer #(.select(2), .width(4), .enable("false")) multiplexer_2 (
    .in0(rA), .in3(4'b1111), .out(dstM), .sel(dstM_ctrl));  // open: in1, in2
  // Probe on srcA_ctrl
  Multiplexer #(.select(2), .width(4), .enable("false")) multiplexer_3 (
    .in0(rA), .in1(4'b0100), .in3(4'b1111), .out(srcA), .sel(srcA_ctrl));  // open: in2
  ROM #(.addrWidth(4), .dataWidth(2)) u_srcA_ctrl (.addr(icode), .data(srcA_ctrl));
  ROM #(.addrWidth(4), .dataWidth(2)) u_srcB_ctrl (.addr(icode), .data(srcB_ctrl));
  // Probe on srcB_ctrl
  Multiplexer #(.select(2), .width(4), .enable("false")) multiplexer_4 (
    .in0(rB), .in1(4'b0100), .in3(4'b1111), .out(srcB), .sel(srcB_ctrl));  // open: in2
  // Probe on srcA_ctrl
  // Probe on srcB_ctrl

  // Notes on the sheet:
  //   Used only for conditional move
  //   contents of rom_1 (hex, n*v repeats v):
  //   3 3 0 0 3 3 0 3 4*1
  //   contents of rom_2 (hex, n*v repeats v):
  //   5*3 0 5*3
  //   0: rB, 3: F
  //   0: rA, 3: F
  //   TODO: Modifica los ROMs para controlar cuales deben ser los source de valA y valB, y los dest de valE y valM
  //   ****_ctrl==3 selecciona F, que significa que no se usa registro
  //   contents of srcA_ctrl (hex, n*v repeats v):
  //   3 3 0 3 0 3 0 3 3 1 0 1
  //   contents of srcB_ctrl (hex, n*v repeats v):
  //   4*3 0 0 0 3 4*1
  //   0: rA, 1: RRSP
  //   0: rB, 1: RRSP
endmodule

module Fetch (
  input  [7:0] I_0,
  input  [7:0] I_1,
  input  [7:0] I_2,
  input  [7:0] I_3,
  output [3:0] icode,
  output [3:0] ifun,
  output [3:0] rA,
  output [3:0] rB,
  output [15:0] valC
);

  wire need_regids, need_valC;
  wire [15:0] buffer_1_out, multiplexer_1_out;

  ROM #(.addrWidth(4), .dataWidth(1)) rom_1 (.addr(I_0[7:4]));  // open: data
  ROM #(.addrWidth(4), .dataWidth(1)) rom_2 (.addr(I_0[7:4]));  // open: data
  Multiplexer #(.width(16), .enable("false")) multiplexer_1 (
    .in0({I_2, I_1}), .in1({I_3, I_2}), .out(multiplexer_1_out), .sel(need_regids));
  // Probe on need_regids
  // Probe on need_valC
  // Buffer buffer_1 has open pins: in=open, out=buffer_1_out
  // Probe on valC
  Multiplexer #(.width(16), .enable("false")) multiplexer_2 (
    .in0(buffer_1_out), .in1(multiplexer_1_out), .out(valC), .sel(need_valC));

  assign icode = I_0[7:4];
  assign ifun = I_0[3:0];
  assign rA = I_1[7:4];
  assign rB = I_1[3:0];

  // Notes on the sheet:
  //   contents of rom_1 (hex, n*v repeats v):
  //   0 0 5*1 0 0 0 1 1
  //   contents of rom_2 (hex, n*v repeats v):
  //   0 0 0 1 1 1 0 1 1
  //   ?
  //   need_regids=1 si y solo si la instrucción tiene los campos rA,rB
  //   need_valC=1 si y solo si la instrucción contiene el campo valC (value V, offset D or address Dest)
  //   xxxx
  //   TODO: Edita los ROMs need_regids y need_valC para obtener la señal correcta basado en icode
  //   TODO: Usa Wiring/Splitter to extraer los campos rA, rB y valC de la instrucción
  //   Debes estar conciente que valC es I_2:I_1 o I_3:I_2 dependiendo de need_regids
  //   buffer_1 drives only 0 and floats otherwise
endmodule

module PC_Update (
  input  [3:0] icode,
  input  Cnd,
  input  [15:0] valC,
  input  [15:0] valM,
  input  [15:0] oldPC,
  output HLT,
  output [15:0] valP,
  output [15:0] newPC
);

  wire [1:0] jmp_ctrl;
  wire [3:0] PC_incr;
  wire [15:0] bit_extender_1_out, multiplexer_2_out;

  // Probe on PC_incr
  // Probe on icode
  ROM #(.addrWidth(4), .dataWidth(4)) rom_1 (.addr(icode), .data(PC_incr));
  assign bit_extender_1_out = {{12{1'b0}}, PC_incr};  // Bit_Extender bit_extender_1
  Adder #(.width(16)) adder_1 (.a(bit_extender_1_out), .b(oldPC), .out(valP));  // open: cin, cout
  Comparator #(.width(4)) comparator_1 (.a(icode), .b(4'b0000), .eq(HLT));  // open: gt, lt
  ROM #(.addrWidth(4), .dataWidth(2)) rom_2 (.addr(icode), .data(jmp_ctrl));
  Multiplexer #(.select(2), .width(16), .enable("false")) multiplexer_1 (
    .in0(valP), .in1(multiplexer_2_out), .in2(valC), .in3(valM), .out(newPC), .sel(jmp_ctrl));
  Multiplexer #(.width(16), .enable("false")) multiplexer_2 (
    .in0(valP), .in1(valC), .out(multiplexer_2_out), .sel(Cnd));

  // Other names for the same wires on the sheet: PC[15:0] = oldPC

  // Notes on the sheet:
  //   OUTPUTS:
  //   INPUTS:
  //   TODO: Asigna la cantidad correcta de inc para cada icode
  //   PC=PC+inc
  //   AUXILIARY COMPONENTS:
  //   contents of rom_1 (hex, n*v repeats v):
  //   0 1 2 4 4 4 2 3 3 1 2 2
  //   HLT=1 iff icode==0
  //   contents of rom_2 (hex, n*v repeats v):
  //   7*0 1 2 3
  //   TODO: controlar el PC cuando hay jump, call o ret
  //   newPC debe ser valP, a menos que haya un jump, call o ret
endmodule

module SimpleCounter (
  input  CLK,
  input  RST,
  output [15:0] CountOut
);

  wire [15:0] adder_1_out;

  Register #(.width(16)) register_1 (.D(adder_1_out), .en(1'b1), .clk(CLK), .Q(CountOut), .clr(RST));
  Adder #(.width(16)) adder_1 (.a(16'h1), .b(CountOut), .out(adder_1_out));  // open: cin, cout

  // Notes on the sheet:
  //   Nothing to edit here, just a simple clock cycles counter
endmodule
